// Logisim project SE2_1610300c14_刘铭尧_cpu.circ as structural Verilog
module main (
  input  in_1,
  input  in_2
);

  wire alu_11_1_overflow, alu_11_1_zero, and_1_out, not_1_out, not_2_out, op_ctr_1_alusrc, op_ctr_1_branch,
       op_ctr_1_extop, op_ctr_1_jump, op_ctr_1_memwr, op_ctr_1_mtoreg, op_ctr_1_regdst, op_ctr_1_regwr;
  wire [2:0] op_ctr_1_aluctr;
  wire [4:0] insanalyse_1_rd, insanalyse_1_rs, insanalyse_1_rt, multiplexer_1_out;
  wire [5:0] insanalyse_1_funct, insanalyse_1_op;
  wire [15:0] insanalyse_1_immediate16;
  wire [25:0] insanalyse_1_immediate26;
  wire [31:0] alu_11_1_result, disp, fetch_ir_1_in_pc, fetch_ir_1_ir_addre, main_1_reg1, main_1_reg2_2,
       multiplexer_2_out, n16_32extend_1_out32, PC_q, ram_1_data, rom_1_data;

  ROM #(.addrWidth(10), .dataWidth(32)) rom_1 (.addr(fetch_ir_1_ir_addre[9:0]), .data(rom_1_data), .sel(1'b1));
  InsAnalyse insanalyse_1 (
    .Ins(rom_1_data), .OP(insanalyse_1_op), .Rs(insanalyse_1_rs), .Rt(insanalyse_1_rt), .Rd(insanalyse_1_rd),
    .funct(insanalyse_1_funct), .Immediate16(insanalyse_1_immediate16), .Immediate26(insanalyse_1_immediate26));  // open: Shamt
  fetch_IR fetch_ir_1 (
    .Target25_0(insanalyse_1_immediate26), .pc_out(PC_q), .imm16(insanalyse_1_immediate16),
    .Branch(op_ctr_1_branch), .Zero(alu_11_1_zero), .Jump(op_ctr_1_jump), .IR_addre(fetch_ir_1_ir_addre),
    .in_pc(fetch_ir_1_in_pc));
  op_ctr op_ctr_1 (
    .op(insanalyse_1_op), .func(insanalyse_1_funct), .Branch(op_ctr_1_branch), .Jump(op_ctr_1_jump),
    .RegDst(op_ctr_1_regdst), .ALUSrc(op_ctr_1_alusrc), .MtoReg(op_ctr_1_mtoreg), .RegWr(op_ctr_1_regwr),
    .MemWr(op_ctr_1_memwr), .ExtOp(op_ctr_1_extop), .ALUctr(op_ctr_1_aluctr));
  Multiplexer #(.width(5), .enable("false")) multiplexer_1 (
    .in0(insanalyse_1_rt), .in1(insanalyse_1_rd), .out(multiplexer_1_out), .sel(op_ctr_1_regdst));
  Register #(.width(32)) PC (.D(fetch_ir_1_in_pc), .en(1'b1), .Q(PC_q), .clk(in_2), .clr(in_1));
  and and_1 (and_1_out, op_ctr_1_regwr, not_1_out);
  _16_32extend u_16_32extend_1 (.in16(insanalyse_1_immediate16), .ExtOp(op_ctr_1_extop), .out32(n16_32extend_1_out32));
  regfile_cpu_main main_1 (
    .Reg1_num(insanalyse_1_rs), .Reg2(insanalyse_1_rt), .Write_Reg_num(multiplexer_1_out), .Din(disp),
    .Write_Enable(and_1_out), .Clock(in_2), .Reg1(main_1_reg1), .Reg2_2(main_1_reg2_2));  // open: s0_Value, s1_Value, s2_Value, ra_Value, v0_Value, a0_Value, rst
  Counter #(.width(32), .max('hffffffff)) count (.clk(in_2));  // open: load, D, count, Q, carry, clr
  not not_1 (not_1_out, alu_11_1_overflow);
  alu_11 alu_11_1 (
    .zero(alu_11_1_zero), .Overflow(alu_11_1_overflow), .Result(alu_11_1_result), .A(main_1_reg1),
    .B(multiplexer_2_out), .ALUctr(op_ctr_1_aluctr));
  Multiplexer #(.width(32), .enable("false")) multiplexer_2 (
    .in0(main_1_reg2_2), .in1(n16_32extend_1_out32), .out(multiplexer_2_out), .sel(op_ctr_1_alusrc));
  not not_2 (not_2_out, op_ctr_1_memwr);
  RAM #(.addrWidth(10), .dataWidth(32), .bus("separate")) ram_1 (
    .addr(alu_11_1_result[9:0]), .din(main_1_reg2_2), .data(ram_1_data), .str(op_ctr_1_memwr), .sel(1'b1),
    .clk(in_2), .ld(not_2_out), .clr(1'b0));
  Multiplexer #(.width(32), .enable("false")) multiplexer_3 (
    .in0(alu_11_1_result), .in1(ram_1_data), .out(disp), .sel(op_ctr_1_mtoreg));

  // Other names for the same wires on the sheet: clk = in_2

  // Notes on the sheet:
  //   contents of rom_1 (hex, n*v repeats v):
  //   8c110001 8c120002 2519820 ac130003 2519822 ac130004 2519823 ac130005 251982a ac130006 251982b
  //   ac130007 12320001 8000c00 ac120008 8000c02
endmodule

module InsAnalyse (
  input  [31:0] Ins,
  output [5:0] OP,
  output [4:0] Rs,
  output [4:0] Rt,
  output [4:0] Rd,
  output [4:0] Shamt,
  output [5:0] funct,
  output [15:0] Immediate16,
  output [25:0] Immediate26
);


  assign funct = Ins[5:0];
  assign Immediate16 = Ins[15:0];
  assign Immediate26 = Ins[25:0];
  assign OP = Ins[31:26];
  assign Rd = Ins[15:11];
  assign Rs = Ins[25:21];
  assign Rt = Ins[20:16];
  assign Shamt = Ins[10:6];
endmodule

module IR (
  input  Rst,
  input  IE,
  input  IEW,
  input  INMW,
  input  [3:0] INM,
  input  IR0,
  input  IR1,
  input  IR2,
  input  IR3,
  output [1:0] IRNUM,
  output IR
);

  wire and_1_out, and_2_out, and_3_out, and_4_out, Clk, not_1_out, not_2_out, not_3_out, not_4_out,
       priority_encoder_1_gs, register_1_q, register_2_q, register_3_q, register_4_q, register_5_q,
       register_6_q, register_7_q, register_8_q, register_9_q;

  Clock u_Clk (.out(Clk));
  Register #(.width(1)) register_1 (.D(1'b1), .en(1'b1), .Q(register_1_q), .clk(IR0), .clr(Rst));
  Register #(.width(1)) register_2 (.D(1'b1), .en(1'b1), .Q(register_2_q), .clk(IR1), .clr(Rst));
  Register #(.width(1)) register_3 (.D(1'b1), .en(1'b1), .Q(register_3_q), .clk(IR2), .clr(Rst));
  Register #(.width(1)) register_4 (.D(1'b1), .en(1'b1), .Q(register_4_q), .clk(IR3), .clr(Rst));
  Register #(.width(1)) register_5 (.D(INM[0]), .en(INMW), .Q(register_5_q), .clk(Clk), .clr(Rst));
  not not_1 (not_1_out, register_5_q);
  not not_2 (not_2_out, register_6_q);
  Register #(.width(1)) register_6 (.D(INM[1]), .en(INMW), .Q(register_6_q), .clk(Clk), .clr(Rst));
  not not_3 (not_3_out, register_7_q);
  Register #(.width(1)) register_7 (.D(INM[2]), .en(INMW), .Q(register_7_q), .clk(Clk), .clr(Rst));
  Register #(.width(1)) register_8 (.D(INM[3]), .en(INMW), .Q(register_8_q), .clk(Clk), .clr(Rst));
  not not_4 (not_4_out, register_8_q);
  and and_1 (and_1_out, register_1_q, not_1_out);
  and and_2 (and_2_out, register_2_q, not_2_out);
  and and_3 (and_3_out, register_3_q, not_3_out);
  and and_4 (and_4_out, register_4_q, not_4_out);
  Priority_Encoder #(.select(2), .disabled(0)) priority_encoder_1 (
    .in0(and_1_out), .in1(and_2_out), .in2(and_3_out), .in3(and_4_out), .out(IRNUM),
    .gs(priority_encoder_1_gs), .en_in(1'b1));  // open: en_out
  Register #(.width(1)) register_9 (.D(IE), .en(IEW), .Q(register_9_q), .clk(Clk), .clr(Rst));
  and and_5 (IR, priority_encoder_1_gs, register_9_q);
endmodule

// 16ex32
module _16_32extend (
  input  [15:0] in16,
  input  ExtOp,
  output [31:0] out32
);

  Multiplexer #(.enable("false")) multiplexer_1 (.in0(1'b0), .in1(in16[15]), .out(out32[31]), .sel(ExtOp));

  assign out32[30:0] = {{15{out32[31]}}, in16};
endmodule

module op_ctr (
  input  [5:0] op,
  input  [5:0] func,
  output Branch,
  output Jump,
  output RegDst,
  output ALUSrc,
  output MtoReg,
  output RegWr,
  output MemWr,
  output ExtOp,
  output [2:0] ALUctr
);

  wire and_5_out, and_6_out, and_7_out, and_8_out, not_1_out, not_2_out, not_4_out, not_5_out, not_6_out,
       not_7_out, not_9_out, not_10_out, not_11_out, not_12_out, not_13_out, not_14_out;
  wire [2:0] and_10_out, func_ctr_1_aluctr0;

  func_ctr func_ctr_1 (
    .func5(func[5]), .func4(func[4]), .func3(func[3]), .func2(func[2]), .func1(func[1]), .func0(func[0]),
    .ALUctr2(func_ctr_1_aluctr0[2]), .ALUctr1(func_ctr_1_aluctr0[1]), .ALUctr0(func_ctr_1_aluctr0[0]));
  not not_1 (not_1_out, op[3]);
  not not_2 (not_2_out, op[0]);
  not not_3 (RegDst, op[0]);
  not not_4 (not_4_out, op[2]);
  not not_5 (not_5_out, op[1]);
  not not_6 (not_6_out, op[1]);
  not not_7 (not_7_out, op[3]);
  and and_1 (MemWr, op[3], op[1]);
  not not_8 (ExtOp, op[2]);
  not not_9 (not_9_out, op[3]);
  not not_10 (not_10_out, op[2]);
  not not_11 (not_11_out, op[1]);
  not not_12 (not_12_out, op[3]);
  and and_2 (and_10_out[1], op[3], op[2]);
  not not_13 (not_13_out, op[2]);
  not not_14 (not_14_out, op[0]);
  and and_3 (Branch, not_1_out, op[2]);
  and and_4 (Jump, op[1], not_2_out);
  and and_5 (and_5_out, not_4_out, not_5_out);
  and and_6 (and_6_out, op[3], not_6_out);
  and and_7 (and_7_out, op[5], not_7_out);
  and and_8 (and_8_out, not_9_out, not_10_out, not_11_out);
  and and_9 (and_10_out[2], not_12_out, op[2]);
  and and_10 (and_10_out[0], not_13_out, not_14_out);
  or or_1 (RegWr, and_5_out, and_6_out, and_7_out);
  Multiplexer #(.width(3), .enable("false")) multiplexer_1 (
    .in0(and_10_out), .in1(func_ctr_1_aluctr0), .out(ALUctr), .sel(and_8_out));

  assign ALUSrc = op[0];
  assign MtoReg = op[1];

  // Notes on the sheet:
  //   Rtype
  //   ALUop2
  //   ALUop1
  //   ALUop0
endmodule

module func_ctr (
  input  func5,
  input  func4,
  input  func3,
  input  func2,
  input  func1,
  input  func0,
  output ALUctr2,
  output ALUctr1,
  output ALUctr0
);

  not not_1 (ALUctr0, func0);

  assign ALUctr1 = func3;
  assign ALUctr2 = func1;
endmodule

// fech_IR
module fetch_IR (
  input  [25:0] Target25_0,
  input  [31:0] pc_out,
  input  [15:0] imm16,
  input  Jump,
  input  Branch,
  input  Zero,
  output [31:0] IR_addre,
  output [31:0] in_pc
);

  wire and_1_out;
  wire [31:0] adder_1_out, adder_2_out, multiplexer_1_out, n16_32extend_1_out32;

  _16_32extend u_16_32extend_1 (.in16(imm16), .ExtOp(1'b1), .out32(n16_32extend_1_out32));
  Adder #(.width(32)) adder_1 (.a(pc_out), .b(32'h1), .out(adder_1_out));  // open: cin, cout
  Adder #(.width(32)) adder_2 (.a(adder_1_out), .b(n16_32extend_1_out32), .out(adder_2_out));  // open: cin, cout
  Multiplexer #(.width(32), .enable("false")) multiplexer_1 (
    .in0(adder_1_out), .in1(adder_2_out), .out(multiplexer_1_out), .sel(and_1_out));
  and and_1 (and_1_out, Branch, Zero);
  Multiplexer #(.width(32), .enable("false")) multiplexer_2 (
    .in0(multiplexer_1_out), .in1({pc_out[31:26], Target25_0}), .out(in_pc), .sel(Jump));

  assign IR_addre = pc_out;

  // Notes on the sheet:
  //   Target25:0
  //   pc31:28
endmodule
