// Logisim project alu-cpu-11.circ as structural Verilog: 9 circuits, main circuit adder32
module main (
);

  // AND_Gate and_1 is placed but not wired
endmodule

// add
module fulladder (
  input  x,
  input  y,
  input  cin,
  output sum,
  output cout
);

  wire and_1_out, and_2_out, and_3_out, and_4_out, and_5_out, and_6_out, and_7_out, not_1_out, not_2_out,
       not_3_out, not_4_out, not_5_out, not_6_out;

  not not_1 (not_1_out, x);
  not not_2 (not_2_out, y);
  not not_3 (not_3_out, x);
  not not_4 (not_4_out, cin);
  not not_5 (not_5_out, y);
  not not_6 (not_6_out, cin);
  and and_1 (and_1_out, y, cin);
  and and_2 (and_2_out, x, cin);
  and and_3 (and_3_out, x, y);
  and and_4 (and_4_out, not_1_out, not_2_out, cin);
  and and_5 (and_5_out, not_3_out, y, not_4_out);
  and and_6 (and_6_out, x, not_5_out, not_6_out);
  and and_7 (and_7_out, x, y, cin);
  or or_1 (cout, and_1_out, and_2_out, and_3_out);
  or or_2 (sum, and_4_out, and_5_out, and_6_out, and_7_out);
endmodule

module fulladder2 (
  input  x,
  input  y,
  input  c,
  output s,
  output co
);

  wire and_1_out, and_2_out, and_3_out;

  xor odd_parity_1 (s, x, y, c);
  and and_1 (and_1_out, x, y);
  and and_2 (and_2_out, x, c);
  and and_3 (and_3_out, y, c);
  or or_1 (co, and_1_out, and_2_out, and_3_out);
endmodule

// add4
module add_4bit (
  input  Cin,
  input  [3:0] A,
  input  [3:0] B,
  output [3:0] F,
  output Cout_1,
  output Cout
);

  wire fulladder_3_cout, fulladder_4_cout;

  fulladder fulladder_1 (.x(A[3]), .y(B[3]), .cin(Cout_1), .sum(F[3]), .cout(Cout));
  fulladder fulladder_2 (.x(A[2]), .y(B[2]), .cin(fulladder_3_cout), .sum(F[2]), .cout(Cout_1));
  fulladder fulladder_3 (.x(A[1]), .y(B[1]), .cin(fulladder_4_cout), .sum(F[1]), .cout(fulladder_3_cout));
  fulladder fulladder_4 (.x(A[0]), .y(B[0]), .cin(Cin), .sum(F[0]), .cout(fulladder_4_cout));
endmodule

// add32
module adder32 (
  input  Cin,
  input  [31:0] A,
  input  [31:0] B,
  input  [31:0] in_4,
  input  [31:0] in_5,
  input  [3:0] aluop,
  output [31:0] F,
  output ZF,
  output SF,
  output OF,
  output CF,
  output Cout,
  output Signed_Overflow,
  output UnSigned__Overflow,
  output Equal,
  output [31:0] out_16,
  output [31:0] out_17
);

  wire add_4bit_1_cout_1, add_4bit_2_cout, add_4bit_3_cout, add_4bit_4_cout, add_4bit_5_cout,
       add_4bit_6_cout, add_4bit_7_cout, add_4bit_8_cout, fulladder_1_cout, fulladder_3_cout,
       fulladder_4_cout, fulladder_5_cout;

  xor xor_1 (OF, add_4bit_1_cout_1, Cout);
  xor xor_2 (CF, Cin, Cout);
  add_4bit add_4bit_1 (
    .Cout_1(add_4bit_1_cout_1), .Cout(Cout), .Cin(add_4bit_2_cout), .F(F[31:28]), .A(A[31:28]), .B(B[31:28]));
  add_4bit add_4bit_2 (
    .Cout(add_4bit_2_cout), .Cin(add_4bit_3_cout), .F(F[27:24]), .A(A[27:24]), .B(B[27:24]));  // open: Cout_1
  add_4bit add_4bit_3 (
    .Cout(add_4bit_3_cout), .Cin(add_4bit_4_cout), .F(F[23:20]), .A(A[23:20]), .B(B[23:20]));  // open: Cout_1
  add_4bit add_4bit_4 (
    .Cout(add_4bit_4_cout), .Cin(add_4bit_5_cout), .F(F[19:16]), .A(A[19:16]), .B(B[19:16]));  // open: Cout_1
  add_4bit add_4bit_5 (
    .Cout(add_4bit_5_cout), .Cin(add_4bit_6_cout), .F(F[15:12]), .A(A[15:12]), .B(B[15:12]));  // open: Cout_1
  Comparator #(.width(32)) comparator_1 (.a({32{1'b0}}), .b(F), .eq(ZF));  // open: gt, lt
  add_4bit add_4bit_6 (
    .Cout(add_4bit_6_cout), .Cin(add_4bit_7_cout), .F(F[11:8]), .A(A[11:8]), .B(B[11:8]));  // open: Cout_1
  add_4bit add_4bit_7 (
    .Cout(add_4bit_7_cout), .Cin(add_4bit_8_cout), .F(F[7:4]), .A(A[7:4]), .B(B[7:4]));  // open: Cout_1
  add_4bit add_4bit_8 (.Cout(add_4bit_8_cout), .Cin(Cin), .F(F[3:0]), .A(A[3:0]), .B(B[3:0]));  // open: Cout_1
  fulladder fulladder_1 (.cout(fulladder_1_cout));  // open: x, y, cin, sum
  fulladder fulladder_2 (.cin(fulladder_4_cout));  // open: x, y, sum, cout
  fulladder fulladder_3 (.cin(fulladder_5_cout), .cout(fulladder_3_cout));  // open: x, y, sum
  fulladder fulladder_4 (.cin(fulladder_3_cout), .cout(fulladder_4_cout));  // open: x, y, sum
  fulladder fulladder_5 (.cout(fulladder_5_cout));  // open: x, y, cin, sum

  assign SF = F[31];

  // Other names for the same wires on the sheet: OF_t = Signed_Overflow; Result[31:0] = out_16;
  //   Result2[31:0] = out_17; s[3:0] = aluop; UOF = UnSigned__Overflow; x[31:0] = in_4; y[31:0] = in_5

  // Notes on the sheet:
  //   输入端
  //   感谢华中科技大学计算机学院的帮助和支持！
  //   输出端
endmodule

module alu_11 (
  input  [31:0] A,
  input  [31:0] B,
  input  [2:0] ALUctr,
  output zero,
  output Overflow,
  output [31:0] Result
);

  wire ALU_cf, alu_ctr_1_ovctr, alu_ctr_1_sigctr, alu_ctr_1_subctr, ALU_of, ALU_sf, multiplexer_1_out,
       not_1_out, xor_1_out, xor_2_out;
  wire [1:0] alu_ctr_1_opctr0;
  wire [31:0] ALU_f, multiplexer_2_out, or_32_1_out, xor_32_1_y;

  Multiplexer #(.enable("false")) multiplexer_1 (
    .in0(not_1_out), .in1(xor_1_out), .out(multiplexer_1_out), .sel(alu_ctr_1_sigctr));
  xor xor_1 (xor_1_out, ALU_sf, ALU_of);
  xor xor_2 (xor_2_out, ALU_cf, alu_ctr_1_subctr);
  not not_1 (not_1_out, xor_2_out);
  adder32 ALU (
    .SF(ALU_sf), .OF(ALU_of), .CF(ALU_cf), .F(ALU_f), .A(A), .B(xor_32_1_y), .ZF(zero), .Cin(alu_ctr_1_subctr));  // open: Cout, in_4, in_5, aluop, out_16, out_17, Signed_Overflow, UnSigned__Overflow, Equal
  XOR_32 xor_32_1 (.Y(xor_32_1_y), .X(B), .SUBctr(alu_ctr_1_subctr));
  ALU_CTR alu_ctr_1 (
    .ALUctr2(ALUctr[2]), .ALUctr1(ALUctr[1]), .ALUctr0(ALUctr[0]), .SUBctr(alu_ctr_1_subctr),
    .OVctr(alu_ctr_1_ovctr), .SIGctr(alu_ctr_1_sigctr), .OPctr1(alu_ctr_1_opctr0[1]),
    .OPctr0(alu_ctr_1_opctr0[0]));
  and and_1 (Overflow, ALU_of, alu_ctr_1_ovctr);
  OR_32 or_32_1 (.A(A), .B(B), .out(or_32_1_out));
  Multiplexer #(.width(32), .enable("false")) multiplexer_2 (
    .in0({32{1'b0}}), .in1(32'h1), .out(multiplexer_2_out), .sel(multiplexer_1_out));
  Multiplexer #(.select(2), .width(32), .enable("false")) multiplexer_3 (
    .in0(ALU_f), .in1(or_32_1_out), .in2(multiplexer_2_out), .out(Result), .sel(alu_ctr_1_opctr0));  // open: in3

  // Notes on the sheet:
  //   less
  //   F
  //   OPctr
endmodule

module XOR_32 (
  input  [31:0] X,
  input  SUBctr,
  output [31:0] Y
);

  xor xor_1 (Y[31], X[31], SUBctr);
  xor xor_2 (Y[30], X[30], SUBctr);
  xor xor_3 (Y[29], X[29], SUBctr);
  xor xor_4 (Y[28], X[28], SUBctr);
  xor xor_5 (Y[27], X[27], SUBctr);
  xor xor_6 (Y[26], X[26], SUBctr);
  xor xor_7 (Y[25], X[25], SUBctr);
  xor xor_8 (Y[24], X[24], SUBctr);
  xor xor_9 (Y[23], X[23], SUBctr);
  xor xor_10 (Y[21], X[21], SUBctr);
  xor xor_11 (Y[22], X[22], SUBctr);
  xor xor_12 (Y[19], X[19], SUBctr);
  xor xor_13 (Y[20], X[20], SUBctr);
  xor xor_14 (Y[17], X[17], SUBctr);
  xor xor_15 (Y[18], X[18], SUBctr);
  xor xor_16 (Y[16], X[16], SUBctr);
  xor xor_17 (Y[15], X[15], SUBctr);
  xor xor_18 (Y[14], X[14], SUBctr);
  xor xor_19 (Y[13], X[13], SUBctr);
  xor xor_20 (Y[12], X[12], SUBctr);
  xor xor_21 (Y[11], X[11], SUBctr);
  xor xor_22 (Y[9], X[9], SUBctr);
  xor xor_23 (Y[10], X[10], SUBctr);
  xor xor_24 (Y[7], X[7], SUBctr);
  xor xor_25 (Y[8], X[8], SUBctr);
  xor xor_26 (Y[5], X[5], SUBctr);
  xor xor_27 (Y[6], X[6], SUBctr);
  xor xor_28 (Y[3], X[3], SUBctr);
  xor xor_29 (Y[4], X[4], SUBctr);
  xor xor_30 (Y[1], X[1], SUBctr);
  xor xor_31 (Y[2], X[2], SUBctr);
  xor xor_32 (Y[0], X[0], SUBctr);
endmodule

module ALU_CTR (
  input  ALUctr2,
  input  ALUctr1,
  input  ALUctr0,
  output SUBctr,
  output OVctr,
  output SIGctr,
  output OPctr1,
  output OPctr0
);

  wire not_1_out, not_2_out;

  not not_1 (not_1_out, ALUctr1);
  and and_1 (OPctr1, ALUctr2, ALUctr1);
  not not_2 (not_2_out, ALUctr2);
  and and_2 (OVctr, not_1_out, ALUctr0);
  and and_3 (OPctr0, not_2_out, ALUctr1);

  assign SIGctr = ALUctr0;
  assign SUBctr = ALUctr2;
endmodule

// or-32
module OR_32 (
  input  [31:0] B,
  input  [31:0] A,
  output [31:0] out
);

  or or_1 (out[30], A[30], B[30]);
  or or_2 (out[31], A[31], B[31]);
  or or_3 (out[29], A[29], B[29]);
  or or_4 (out[28], A[28], B[28]);
  or or_5 (out[27], A[27], B[27]);
  or or_6 (out[26], A[26], B[26]);
  or or_7 (out[24], A[24], B[24]);
  or or_8 (out[25], A[25], B[25]);
  or or_9 (out[22], A[22], B[22]);
  or or_10 (out[23], A[23], B[23]);
  or or_11 (out[21], A[21], B[21]);
  or or_12 (out[20], A[20], B[20]);
  or or_13 (out[19], A[19], B[19]);
  or or_14 (out[18], A[18], B[18]);
  or or_15 (out[16], A[16], B[16]);
  or or_16 (out[17], A[17], B[17]);
  or or_17 (out[14], A[14], B[14]);
  or or_18 (out[15], A[15], B[15]);
  or or_19 (out[12], A[12], B[12]);
  or or_20 (out[13], A[13], B[13]);
  or or_21 (out[10], A[10], B[10]);
  or or_22 (out[11], A[11], B[11]);
  or or_23 (out[9], A[9], B[9]);
  or or_24 (out[8], A[8], B[8]);
  or or_25 (out[7], A[7], B[7]);
  or or_26 (out[6], A[6], B[6]);
  or or_27 (out[5], A[5], B[5]);
  or or_28 (out[4], A[4], B[4]);
  or or_29 (out[2], A[2], B[2]);
  or or_30 (out[3], A[3], B[3]);
  or or_31 (out[0], A[0], B[0]);
  or or_32 (out[1], A[1], B[1]);
endmodule
