// Logisim project 实验1-1.circ as structural Verilog
module ADDR (
  input  A,
  input  B,
  input  Cin,
  output S,
  output Cout
);

  wire and_1_out, and_2_out, and_3_out, and_4_out, and_5_out, and_6_out, and_7_out, not_1_out, not_2_out,
       not_3_out, not_4_out, not_5_out, not_6_out;

  not not_1 (not_1_out, A);
  not not_2 (not_2_out, B);
  not not_3 (not_3_out, A);
  not not_4 (not_4_out, Cin);
  not not_5 (not_5_out, B);
  not not_6 (not_6_out, Cin);
  and and_1 (and_1_out, B, Cin);
  and and_2 (and_2_out, A, Cin);
  and and_3 (and_3_out, A, B);
  and and_4 (and_4_out, not_1_out, not_2_out, Cin);
  and and_5 (and_5_out, not_3_out, B, not_4_out);
  and and_6 (and_6_out, A, not_5_out, not_6_out);
  and and_7 (and_7_out, A, B, Cin);
  or or_1 (Cout, and_1_out, and_2_out, and_3_out);
  or or_2 (S, and_4_out, and_5_out, and_6_out, and_7_out);
endmodule

module ADDR4 (
  input  Cin,
  input  [3:0] A,
  input  [3:0] B,
  output [3:0] out_4,
  output out_5,
  output Cout
);

  wire addr_3_cout, addr_4_cout;

  ADDR addr_1 (.A(A[3]), .B(B[3]), .Cin(out_5), .S(out_4[3]), .Cout(Cout));
  ADDR addr_2 (.A(A[2]), .B(B[2]), .Cin(addr_3_cout), .S(out_4[2]), .Cout(out_5));
  ADDR addr_3 (.A(A[1]), .B(B[1]), .Cin(addr_4_cout), .S(out_4[1]), .Cout(addr_3_cout));
  ADDR addr_4 (.A(A[0]), .B(B[0]), .Cin(Cin), .S(out_4[0]), .Cout(addr_4_cout));
endmodule
