// Logisim project 实验1-2.circ as structural Verilog
module ADDR (
  input  A,
  input  B,
  input  Cin,
  output S,
  output Cout
);

  wire and_1_out, and_2_out, and_3_out, and_4_out, and_5_out, and_6_out, and_7_out, not_1_out, not_2_out,
       not_3_out, not_4_out, not_5_out, not_6_out;

  not not_1 (not_1_out, A);
  not not_2 (not_2_out, B);
  not not_3 (not_3_out, A);
  not not_4 (not_4_out, Cin);
  not not_5 (not_5_out, B);
  not not_6 (not_6_out, Cin);
  and and_1 (and_1_out, B, Cin);
  and and_2 (and_2_out, A, Cin);
  and and_3 (and_3_out, A, B);
  and and_4 (and_4_out, not_1_out, not_2_out, Cin);
  and and_5 (and_5_out, not_3_out, B, not_4_out);
  and and_6 (and_6_out, A, not_5_out, not_6_out);
  and and_7 (and_7_out, A, B, Cin);
  or or_1 (Cout, and_1_out, and_2_out, and_3_out);
  or or_2 (S, and_4_out, and_5_out, and_6_out, and_7_out);
endmodule

module ADDR4 (
  input  Cin,
  input  [3:0] A,
  input  [3:0] B,
  output [3:0] F,
  output Cout_1,
  output Cout
);

  wire addr_3_cout, addr_4_cout;

  ADDR addr_1 (.A(A[3]), .B(B[3]), .Cin(Cout_1), .S(F[3]), .Cout(Cout));
  ADDR addr_2 (.A(A[2]), .B(B[2]), .Cin(addr_3_cout), .S(F[2]), .Cout(Cout_1));
  ADDR addr_3 (.A(A[1]), .B(B[1]), .Cin(addr_4_cout), .S(F[1]), .Cout(addr_3_cout));
  ADDR addr_4 (.A(A[0]), .B(B[0]), .Cin(Cin), .S(F[0]), .Cout(addr_4_cout));
endmodule

module ADDR32 (
  input  in_1,
  input  [31:0] A,
  input  [31:0] B,
  output Cout,
  output Cout_2,
  output Cout_3,
  output Cout_4
);

  wire addr4_2_cout, addr4_3_cout, addr4_4_cout, addr4_5_cout, addr4_6_cout, addr4_7_cout, addr4_8_cout;

  ADDR4 addr4_1 (.Cout(Cout_4), .A(A[31:28]), .B(B[31:28]), .Cin(addr4_2_cout));  // open: Cout_1, F
  ADDR4 addr4_2 (.Cout(addr4_2_cout), .A(A[27:24]), .B(B[27:24]), .Cin(addr4_3_cout));  // open: Cout_1, F
  ADDR4 addr4_3 (.Cout(addr4_3_cout), .A(A[23:20]), .B(B[23:20]), .Cin(addr4_4_cout));  // open: Cout_1, F
  ADDR4 addr4_4 (.Cout(addr4_4_cout), .A(A[19:16]), .B(B[19:16]), .Cin(addr4_5_cout));  // open: Cout_1, F
  ADDR4 addr4_5 (.Cout(addr4_5_cout), .A(A[15:12]), .B(B[15:12]), .Cin(addr4_6_cout));  // open: Cout_1, F
  ADDR4 addr4_6 (.Cout(addr4_6_cout), .A(A[11:8]), .B(B[11:8]), .Cin(addr4_7_cout));  // open: Cout_1, F
  ADDR4 addr4_7 (.Cout(addr4_7_cout), .A(A[7:4]), .B(B[7:4]), .Cin(addr4_8_cout));  // open: Cout_1, F
  ADDR4 addr4_8 (.Cout(addr4_8_cout), .A(A[3:0]), .B(B[3:0]), .Cin(in_1));  // open: Cout_1, F
endmodule
