// Logisim project 实验2-1.circ as structural Verilog: 1 circuit, main circuit main
module main (
);

  wire undriven_2, undriven_3;
  wire [7:0] decoder_1_out24;
  wire [7:7] decoder_1_out0;
  wire [31:0] register_1_q, register_2_q, register_3_q, register_4_q, register_5_q, register_6_q,
       register_7_q, register_8_q, register_9_q, register_10_q, register_11_q, register_12_q, register_13_q,
       register_14_q, register_15_q, register_16_q, register_17_q, register_18_q, register_19_q,
       register_20_q, register_21_q, register_22_q, register_23_q, register_24_q, register_25_q,
       register_26_q, register_27_q, register_28_q, register_29_q, register_30_q, register_31_q,
       register_32_q, undriven;

  Decoder #(.select(5)) decoder_1 (
    .out0(decoder_1_out0[7]), .out1(decoder_1_out0[7]), .out2(decoder_1_out0[7]), .out3(decoder_1_out0[7]),
    .out4(decoder_1_out0[7]), .out5(decoder_1_out0[7]), .out6(decoder_1_out0[7]), .out7(decoder_1_out0[7]),
    .out8(decoder_1_out0[7]), .out9(decoder_1_out0[7]), .out10(decoder_1_out0[7]), .out11(decoder_1_out0[7]),
    .out12(decoder_1_out0[7]), .out13(decoder_1_out0[7]), .out14(decoder_1_out0[7]),
    .out15(decoder_1_out0[7]), .out16(decoder_1_out0[7]), .out17(decoder_1_out0[7]),
    .out18(decoder_1_out0[7]), .out19(decoder_1_out0[7]), .out20(decoder_1_out0[7]),
    .out21(decoder_1_out0[7]), .out22(decoder_1_out0[7]), .out23(decoder_1_out0[7]),
    .out24(decoder_1_out24[0]), .out25(decoder_1_out24[1]), .out26(decoder_1_out24[2]),
    .out27(decoder_1_out24[3]), .out28(decoder_1_out24[4]), .out29(decoder_1_out24[5]),
    .out30(decoder_1_out24[6]), .out31(decoder_1_out24[7]));  // open: sel, en
  Register #(.width(32)) register_1 (
    .D(undriven), .en(decoder_1_out0[7]), .Q(register_1_q), .clk(decoder_1_out0[7]), .clr(undriven_2));
  Register #(.width(32)) register_2 (
    .D(undriven), .en(decoder_1_out0[7]), .Q(register_2_q), .clk(decoder_1_out0[7]), .clr(undriven_3));
  Register #(.width(32)) register_3 (
    .D(undriven), .en(decoder_1_out0[7]), .Q(register_3_q), .clk(decoder_1_out0[7]), .clr(undriven_3));
  Register #(.width(32)) register_4 (
    .D(undriven), .en(decoder_1_out24[0]), .Q(register_4_q), .clk(decoder_1_out0[7]), .clr(undriven_3));
  Register #(.width(32)) register_5 (
    .D(undriven), .en(decoder_1_out0[7]), .Q(register_5_q), .clk(decoder_1_out0[7]), .clr(undriven_3));
  Register #(.width(32)) register_6 (
    .D(undriven), .en(decoder_1_out0[7]), .Q(register_6_q), .clk(decoder_1_out0[7]), .clr(undriven_3));
  Register #(.width(32)) register_7 (
    .D(undriven), .en(decoder_1_out0[7]), .Q(register_7_q), .clk(decoder_1_out0[7]), .clr(undriven_3));
  Register #(.width(32)) register_8 (
    .D(undriven), .en(decoder_1_out0[7]), .Q(register_8_q), .clk(decoder_1_out0[7]), .clr(undriven_3));
  Register #(.width(32)) register_9 (
    .D(undriven), .en(decoder_1_out0[7]), .Q(register_9_q), .clk(decoder_1_out0[7]), .clr(undriven_3));
  Register #(.width(32)) register_10 (
    .D(undriven), .en(decoder_1_out0[7]), .Q(register_10_q), .clk(decoder_1_out0[7]), .clr(undriven_3));
  Register #(.width(32)) register_11 (
    .D(undriven), .en(decoder_1_out24[2]), .Q(register_11_q), .clk(decoder_1_out0[7]), .clr(undriven_3));
  Register #(.width(32)) register_12 (
    .D(undriven), .en(decoder_1_out24[1]), .Q(register_12_q), .clk(decoder_1_out0[7]), .clr(undriven_3));
  Register #(.width(32)) register_13 (
    .D(undriven), .en(decoder_1_out0[7]), .Q(register_13_q), .clk(decoder_1_out0[7]), .clr(undriven_3));
  Register #(.width(32)) register_14 (
    .D(undriven), .en(decoder_1_out0[7]), .Q(register_14_q), .clk(decoder_1_out0[7]), .clr(undriven_3));
  Register #(.width(32)) register_15 (
    .D(undriven), .en(decoder_1_out0[7]), .Q(register_15_q), .clk(decoder_1_out0[7]), .clr(undriven_3));
  Register #(.width(32)) register_16 (
    .D(undriven), .en(decoder_1_out24[3]), .Q(register_16_q), .clk(decoder_1_out0[7]), .clr(undriven_3));
  Register #(.width(32)) register_17 (
    .D(undriven), .en(decoder_1_out0[7]), .Q(register_17_q), .clk(decoder_1_out0[7]), .clr(undriven_3));
  Register #(.width(32)) register_18 (
    .D(undriven), .en(decoder_1_out0[7]), .Q(register_18_q), .clk(decoder_1_out0[7]), .clr(undriven_3));
  Register #(.width(32)) register_19 (
    .D(undriven), .en(decoder_1_out0[7]), .Q(register_19_q), .clk(decoder_1_out0[7]), .clr(undriven_3));
  Register #(.width(32)) register_20 (
    .D(undriven), .en(decoder_1_out24[4]), .Q(register_20_q), .clk(decoder_1_out0[7]), .clr(undriven_3));
  Register #(.width(32)) register_21 (
    .D(undriven), .en(decoder_1_out0[7]), .Q(register_21_q), .clk(decoder_1_out0[7]), .clr(undriven_3));
  Register #(.width(32)) register_22 (
    .D(undriven), .en(decoder_1_out0[7]), .Q(register_22_q), .clk(decoder_1_out0[7]), .clr(undriven_3));
  Register #(.width(32)) register_23 (
    .D(undriven), .en(decoder_1_out0[7]), .Q(register_23_q), .clk(decoder_1_out0[7]), .clr(undriven_3));
  Register #(.width(32)) register_24 (
    .D(undriven), .en(decoder_1_out24[5]), .Q(register_24_q), .clk(decoder_1_out0[7]), .clr(undriven_3));
  Register #(.width(32)) register_25 (
    .D(undriven), .en(decoder_1_out0[7]), .Q(register_25_q), .clk(decoder_1_out0[7]), .clr(undriven_3));
  Register #(.width(32)) register_26 (
    .D(undriven), .en(decoder_1_out0[7]), .Q(register_26_q), .clk(decoder_1_out0[7]), .clr(undriven_3));
  Register #(.width(32)) register_27 (
    .D(undriven), .en(decoder_1_out0[7]), .Q(register_27_q), .clk(decoder_1_out0[7]), .clr(undriven_3));
  Register #(.width(32)) register_28 (
    .D(undriven), .en(decoder_1_out24[6]), .Q(register_28_q), .clk(decoder_1_out0[7]), .clr(undriven_3));
  Register #(.width(32)) register_29 (
    .D(undriven), .en(decoder_1_out0[7]), .Q(register_29_q), .clk(decoder_1_out0[7]), .clr(undriven_3));
  Register #(.width(32)) register_30 (
    .D(undriven), .en(decoder_1_out0[7]), .Q(register_30_q), .clk(decoder_1_out0[7]), .clr(undriven_3));
  Register #(.width(32)) register_31 (
    .D(undriven), .en(decoder_1_out0[7]), .Q(register_31_q), .clk(decoder_1_out0[7]), .clr(undriven_3));
  Register #(.width(32)) register_32 (
    .D(undriven), .en(decoder_1_out24[7]), .Q(register_32_q), .clk(decoder_1_out0[7]), .clr(undriven_3));
  Multiplexer #(.select(5), .width(32)) multiplexer_1 (
    .in0(register_1_q), .in1(register_5_q), .in2(register_6_q), .in3(register_13_q), .in4(register_17_q),
    .in5(register_21_q), .in6(register_25_q), .in7(register_29_q), .in8(register_2_q), .in9(register_8_q),
    .in10(register_7_q), .in11(register_14_q), .in12(register_18_q), .in13(register_22_q),
    .in14(register_26_q), .in15(register_30_q), .in16(register_3_q), .in17(register_10_q),
    .in18(register_9_q), .in19(register_15_q), .in20(register_19_q), .in21(register_23_q),
    .in22(register_27_q), .in23(register_31_q), .in24(register_4_q), .in25(register_12_q),
    .in26(register_11_q), .in27(register_16_q), .in28(register_20_q), .in29(register_24_q),
    .in30(register_28_q), .in31(register_32_q));  // open: out, sel, en
  Multiplexer #(.select(5), .width(32)) multiplexer_2 (
    .in0(register_1_q), .in1(register_5_q), .in2(register_6_q), .in3(register_13_q), .in4(register_17_q),
    .in5(register_21_q), .in6(register_25_q), .in7(register_29_q), .in8(register_2_q), .in9(register_8_q),
    .in10(register_7_q), .in11(register_14_q), .in12(register_18_q), .in13(register_22_q),
    .in14(register_26_q), .in15(register_30_q), .in16(register_3_q), .in17(register_10_q),
    .in18(register_9_q), .in19(register_15_q), .in20(register_19_q), .in21(register_23_q),
    .in22(register_27_q), .in23(register_31_q), .in24(register_4_q), .in25(register_12_q),
    .in26(register_11_q), .in27(register_16_q), .in28(register_20_q), .in29(register_24_q),
    .in30(register_28_q), .in31(register_32_q));  // open: out, sel, en
endmodule
